// Logisim project scaffolding.circ as structural Verilog: 2 circuits, main circuit main
// HALT
module main (
  output [23:0] NUM_PASS,
  output [23:0] NUM_FAIL,
  output DONE,
  output halt
);

  wire CLK, comparator_1_eq, not_1_out, RST;
  wire [4:0] caesar_1_out, rom_1_data, rom_2_data;
  wire [23:0] adder_1_out, stepper_1_value, stepper_2_value;

  Clock clock_1 (.out(CLK));
  Button button_1 (.out(RST));
  STEPPER stepper_1 (.ADVANCE(1'b1), .CLK(CLK), .RST(RST), .VALUE(stepper_1_value), .HALT(DONE));
  ROM #(.addrWidth(24), .dataWidth(5)) rom_1 (.addr(stepper_1_value), .data(rom_1_data));  // open: sel
  STEPPER stepper_2 (.ADVANCE(1'b1), .CLK(CLK), .RST(RST), .VALUE(stepper_2_value), .HALT(DONE));
  CAESAR caesar_1 (.IN(rom_1_data), .OUT(caesar_1_out));
  ROM #(.addrWidth(24), .dataWidth(5)) rom_2 (.addr(stepper_2_value), .data(rom_2_data));  // open: sel
  Comparator #(.width(5)) comparator_1 (.a(caesar_1_out), .b(rom_2_data), .eq(comparator_1_eq));  // open: gt, lt
  not not_1 (not_1_out, comparator_1_eq);
  STEPPER stepper_3 (.ADVANCE(comparator_1_eq), .CLK(CLK), .RST(RST), .VALUE(NUM_PASS), .HALT(DONE));
  STEPPER stepper_4 (.ADVANCE(not_1_out), .CLK(CLK), .RST(RST), .VALUE(NUM_FAIL), .HALT(DONE));
  Adder #(.width(24)) adder_1 (.a(NUM_FAIL), .b(NUM_PASS), .out(adder_1_out));  // open: cin, cout
  TRIGGER trigger_1 (.INPUT(adder_1_out), .TRIGGER(24'h1a), .CLK(CLK), .RST(RST), .TRIGGERED(DONE));

  assign halt = DONE;

  // Notes on the sheet:
  //   Test Inputs
  //   contents of rom_1 (hex, n*v repeats v):
  //   10 6 16 1e 8 e a 1a c 12 13 1b b f 1c 1f 17 7 5 15 14 1d d 9 4 19
  //   Expected Outputs
  //   contents of rom_2 (hex, n*v repeats v):
  //   a 1a c 12 13 1b b f 1c 1f 17 7 5 15 14 1d d 9 4 19 10 6 16 1e 8 e
  //   # Tests:
endmodule

module CAESAR (
  input  [4:0] IN,
  output [4:0] OUT
);

  wire and_1_out, and_2_out, and_3_out, and_4_out, and_5_out, and_6_out, and_7_out, and_8_out, and_9_out,
       and_10_out, and_11_out, and_12_out, and_13_out, and_14_out, and_15_out, and_16_out, and_17_out,
       and_18_out, and_19_out, and_20_out, and_21_out, and_22_out, and_23_out, and_24_out, and_25_out,
       and_26_out, and_27_out, and_28_out;
  wire [4:0] not_1_out;

  assign not_1_out = ~IN;  // NOT_Gate not_1, 5 bits wide
  and and_1 (and_1_out, not_1_out[4], IN[2], not_1_out[0]);
  and and_2 (and_2_out, IN[2], not_1_out[1], not_1_out[0]);
  and and_3 (and_3_out, not_1_out[4], IN[3], not_1_out[1]);
  and and_4 (and_4_out, IN[3], IN[2], IN[1]);
  and and_5 (and_5_out, not_1_out[3], not_1_out[2], IN[1]);
  and and_6 (and_6_out, IN[4], not_1_out[3], IN[2], not_1_out[1]);
  and and_7 (and_7_out, not_1_out[4], IN[2], not_1_out[0]);
  and and_8 (and_8_out, not_1_out[3], IN[2], IN[1]);
  and and_9 (and_9_out, not_1_out[3], not_1_out[2], not_1_out[1]);
  and and_10 (and_10_out, not_1_out[2], not_1_out[1], IN[0]);
  and and_11 (and_11_out, not_1_out[2], IN[1], not_1_out[0]);
  and and_12 (and_12_out, IN[4], not_1_out[3], IN[2], IN[0]);
  and and_13 (and_13_out, IN[4], IN[2], IN[1], IN[0]);
  and and_14 (and_14_out, IN[3], IN[0]);
  and and_15 (and_15_out, IN[3], IN[2], not_1_out[1]);
  and and_16 (and_16_out, IN[4], not_1_out[3], IN[1]);
  and and_17 (and_17_out, IN[4], not_1_out[2], IN[1]);
  and and_18 (and_18_out, not_1_out[4], not_1_out[1], IN[0]);
  and and_19 (and_19_out, not_1_out[2], not_1_out[1]);
  and and_20 (and_20_out, IN[4], not_1_out[2]);
  and and_21 (and_21_out, IN[3], not_1_out[1], IN[0]);
  and and_22 (and_22_out, IN[3], IN[1], not_1_out[0]);
  and and_23 (and_23_out, not_1_out[4], IN[1], not_1_out[0]);
  and and_24 (and_24_out, not_1_out[2], IN[1]);
  and and_25 (and_25_out, IN[1], IN[0]);
  and and_26 (and_26_out, not_1_out[4], IN[3], IN[1]);
  and and_27 (and_27_out, not_1_out[4], not_1_out[2], not_1_out[0]);
  and and_28 (and_28_out, IN[4], not_1_out[3], IN[0]);
  or or_1 (OUT[4], and_1_out, and_2_out, and_3_out, and_4_out, and_5_out, and_6_out);
  or or_2 (OUT[3], and_7_out, and_8_out, and_9_out, and_10_out, and_11_out, and_12_out, and_13_out);
  or or_3 (OUT[2], and_14_out, and_15_out, and_16_out, and_17_out, and_18_out);
  or or_4 (OUT[1], and_19_out, and_20_out, and_21_out, and_22_out, and_23_out);
  or or_5 (OUT[0], and_24_out, and_25_out, and_26_out, and_27_out, and_28_out);

  // Notes on the sheet:
  //   bits
  //   negated bits
  //   !X4.X2.!X0
  //   X2.!X1.!X0
  //   !X4.X3.!X1
  //   X3.X2.X1
  //   !X3.!X2.X1
  //   X4.!X3.X2.!X1
  //   !X4.X2.!X0
  //   !X3.X2.X1
  //   !X3.!X2.!X1
  //   !X2.!X1.X0
  //   !X2.X1.!X0
  //   X4.!X3.X2.X0
  //   X4.X2.X1.X0
  //   X3.X0
  //   X3.X2.!X1
  //   X4.!X3.X1
  //   X4.!X2.X1
  //   !X4.!X1.X0
  //   !X2.!X1
  //   X4.!X2
  //   X3.!X1.X0
  //   X3.X1.!X0
  //   !X4.X1.!X0
  //   !X2.X1
  //   X1.X0
  //   !X4.X3.X1
  //   !X4.!X2.!X0
  //   X4.!X3.X0
  //   Y4
  //   Y3
  //   Y2
  //   Y1
  //   Y0
endmodule
