// Logisim project  msm2243.circ as structural Verilog: 4 circuits, main circuit main
// HALT
module main (
  output [23:0] NUM_PASS,
  output [23:0] NUM_FAIL,
  output DONE,
  output TIMEOUT,
  output halt
);

  wire and_1_out, and_2_out, and_3_out, and_4_out, and_5_out, and_6_out, CLK, comparator_1_eq,
       replicator_1_rdy_out, replicator_1_val_out, RST;
  wire [1:0] random_1_out, replicator_1_data_out, rom_1_data, rom_2_data;
  wire [23:0] adder_1_out, stepper_1_value, stepper_2_value, stepper_5_value;

  Clock clock_1 (.out(CLK));
  Button button_1 (.out(RST));
  STEPPER stepper_1 (.ADVANCE(and_1_out), .CLK(CLK), .RST(RST), .VALUE(stepper_1_value), .HALT(halt));
  ROM #(.addrWidth(24), .dataWidth(2)) rom_1 (.addr(stepper_1_value), .data(rom_1_data));  // open: sel
  and and_1 (and_1_out, and_2_out, replicator_1_rdy_out);
  and and_2 (and_2_out, ~halt, random_1_out[1]);  // AND_Gate
  REPLICATOR replicator_1 (
    .RDY_OUT(replicator_1_rdy_out), .CLK(CLK), .RST(RST), .DATA_IN(rom_1_data), .VAL_IN(and_2_out),
    .DATA_OUT(replicator_1_data_out), .VAL_OUT(replicator_1_val_out), .RDY_IN(and_3_out));
  Random #(.width(2)) random_1 (.clk(CLK), .out(random_1_out));  // open: next, clr
  and and_3 (and_3_out, random_1_out[0], ~halt);  // AND_Gate
  and and_4 (and_4_out, replicator_1_val_out, and_3_out);
  STEPPER stepper_2 (.ADVANCE(and_4_out), .CLK(CLK), .RST(RST), .VALUE(stepper_2_value), .HALT(halt));
  ROM #(.addrWidth(24), .dataWidth(2)) rom_2 (.addr(stepper_2_value), .data(rom_2_data));  // open: sel
  Comparator #(.width(2)) comparator_1 (
    .a(replicator_1_data_out), .b(rom_2_data), .eq(comparator_1_eq));  // open: gt, lt
  and and_5 (and_5_out, and_4_out, comparator_1_eq);
  and and_6 (and_6_out, ~comparator_1_eq, and_4_out);  // AND_Gate
  STEPPER stepper_3 (.ADVANCE(and_5_out), .CLK(CLK), .RST(RST), .VALUE(NUM_PASS), .HALT(halt));
  STEPPER stepper_4 (.ADVANCE(and_6_out), .CLK(CLK), .RST(RST), .VALUE(NUM_FAIL), .HALT(halt));
  Adder #(.width(24)) adder_1 (.a(NUM_FAIL), .b(NUM_PASS), .out(adder_1_out));  // open: cin, cout
  STEPPER stepper_5 (.ADVANCE(1'b1), .CLK(CLK), .RST(RST), .VALUE(stepper_5_value), .HALT(halt));
  TRIGGER trigger_1 (.INPUT(adder_1_out), .TRIGGER(24'h18), .CLK(CLK), .RST(RST), .TRIGGERED(DONE));
  TRIGGER trigger_2 (.INPUT(stepper_5_value), .TRIGGER(24'h960), .CLK(CLK), .RST(RST), .TRIGGERED(TIMEOUT));
  or or_1 (halt, DONE, TIMEOUT);

  // Notes on the sheet:
  //   Test Inputs
  //   contents of rom_1 (hex, n*v repeats v):
  //   0 2 3 0 2 2 0 0 2 0 1 3 2 3 2 1 1 0 1 1 3 3 0 1 3 1 0 3 1 2 3 2
  //   Randomly offer/accept data
  //   Expected Outputs
  //   contents of rom_2 (hex, n*v repeats v):
  //   0 0 2 2 1 1 1 4*2 1 3 3 3 0 3 0 0 0 1 1 3 3
  //   # Tests:
  //   Timeout:
endmodule

module REPLICATOR (
  input  [1:0] DATA_IN,
  input  VAL_IN,
  input  CLK,
  input  RST,
  input  RDY_IN,
  output RDY_OUT,
  output [1:0] DATA_OUT,
  output VAL_OUT
);

  wire and_1_out, and_4_out, and_5_out, C_EN, CD1, CD2, COUNT, D_EN, MEMORY, StoredC1, StoredC1_1, StoredC2,
       StoredC2_1;

  D_Flip_Flop d_ff_1 (.clk(CLK), .D(MEMORY), .Q(COUNT), .Qn(MEMORY), .en(and_1_out), .reset(RST));  // open: preset
  and and_1 (and_1_out, RDY_OUT, VAL_IN);
  and and_2 (RDY_OUT, ~StoredC1, ~StoredC2);  // AND_Gate
  and and_3 (D_EN, MEMORY, RDY_OUT);
  not not_1 (VAL_OUT, RDY_OUT);
  D_Flip_Flop d_ff_2 (.clk(CLK), .D(CD1), .Q(StoredC1), .en(C_EN), .reset(RST));  // open: Qn, preset
  D_Flip_Flop d_ff_3 (.clk(CLK), .D(CD2), .Q(StoredC2), .en(C_EN), .reset(RST));  // open: Qn, preset
  MULTIPLEXER multiplexer_1 (.DATA1(StoredC1_1), .DATA2(DATA_IN[0]), .Select(RDY_OUT), .out_4(CD1));
  MULTIPLEXER multiplexer_2 (.DATA1(StoredC2_1), .DATA2(DATA_IN[1]), .Select(RDY_OUT), .out_4(CD2));
  DOWNCOUNTER DOWNCOUNTER (.N2(StoredC2), .N1(StoredC1), .out_3(StoredC2_1), .out_4(StoredC1_1));
  D_Flip_Flop d_ff_4 (.clk(CLK), .D(DATA_IN[0]), .Q(DATA_OUT[0]), .en(D_EN), .reset(RST));  // open: Qn, preset
  D_Flip_Flop d_ff_5 (.clk(CLK), .D(DATA_IN[1]), .Q(DATA_OUT[1]), .en(D_EN), .reset(RST));  // open: Qn, preset
  and and_4 (and_4_out, RDY_IN, VAL_OUT);
  and and_5 (and_5_out, VAL_IN, RDY_OUT, COUNT);
  or or_1 (C_EN, and_4_out, and_5_out);

  // Other names for the same wires on the sheet: D1 = DATA_IN[0]; D2 = DATA_IN[1]; DOUT[1:0] = DATA_OUT;
  //   StoredD1 = DATA_OUT[0]; StoredD2 = DATA_OUT[1]; RIN = RDY_IN; COUNTIS0 = RDY_OUT; ROUT = RDY_OUT; VIN = VAL_IN;
  //   VOUT = VAL_OUT

  // Notes on the sheet:
  //   VARIABLES
  //   INPUT UNIT
  //   INPUT FLOW MANAGING UNIT
  //   COUNT MEMORY UNIT
  //   COUNT MEMORY INPUT FLOW MANAGING UNIT
  //   INPUT UNIT
  //   OUTPUT UNIT
  //   DATA MEMORY UNIT
endmodule

module MULTIPLEXER (
  input  DATA1,
  input  DATA2,
  input  Select,
  output out_4
);

  wire and_1_out, and_2_out;

  and and_1 (and_1_out, DATA1, ~Select);  // AND_Gate
  and and_2 (and_2_out, DATA2, Select);
  or or_1 (out_4, and_1_out, and_2_out);
endmodule

module DOWNCOUNTER (
  input  N2,
  input  N1,
  output out_3,
  output out_4
);

  and and_1 (out_3, N2, N1);
  and and_2 (out_4, N2, ~N1);  // AND_Gate
endmodule
