// Logisim project msm2243.circ as structural Verilog: 2 circuits, main circuit main
// HALT
module main (
  output [23:0] NUM_PASS,
  output [23:0] NUM_FAIL,
  output DONE,
  output TIMEOUT,
  output halt
);

  wire and_1_out, and_2_out, and_3_out, and_4_out, and_5_out, and_6_out, CLK, comparator_1_eq,
       huffdec_1_rdy_out, huffdec_1_val_out, rom_1_data, RST;
  wire [1:0] random_1_out;
  wire [7:0] huffdec_1_char, rom_2_data;
  wire [23:0] adder_1_out, stepper_1_value, stepper_2_value, stepper_5_value;

  Clock clock_1 (.out(CLK));
  Button button_1 (.out(RST));
  STEPPER stepper_1 (.ADVANCE(and_1_out), .CLK(CLK), .RST(RST), .VALUE(stepper_1_value), .HALT(halt));
  ROM #(.addrWidth(24), .dataWidth(1)) rom_1 (.addr(stepper_1_value), .data(rom_1_data));  // open: sel
  and and_1 (and_1_out, and_2_out, huffdec_1_rdy_out);
  and and_2 (and_2_out, ~halt, random_1_out[1]);  // AND_Gate
  HUFFDEC huffdec_1 (
    .CLK(CLK), .RST(RST), .X(rom_1_data), .RDY_OUT(huffdec_1_rdy_out), .VAL_IN(and_2_out),
    .RDY_IN(and_3_out), .VAL_OUT(huffdec_1_val_out), .CHAR(huffdec_1_char));
  Random #(.width(2), .seed(1234)) random_1 (.clk(CLK), .out(random_1_out));  // open: next, clr
  and and_3 (and_3_out, random_1_out[0], ~halt);  // AND_Gate
  and and_4 (and_4_out, huffdec_1_val_out, and_3_out);
  STEPPER stepper_2 (.ADVANCE(and_4_out), .CLK(CLK), .RST(RST), .VALUE(stepper_2_value), .HALT(halt));
  ROM #(.addrWidth(24)) rom_2 (.addr(stepper_2_value), .data(rom_2_data));  // open: sel
  Comparator comparator_1 (.a(huffdec_1_char), .b(rom_2_data), .eq(comparator_1_eq));  // open: gt, lt
  and and_5 (and_5_out, and_4_out, comparator_1_eq);
  and and_6 (and_6_out, ~comparator_1_eq, and_4_out);  // AND_Gate
  STEPPER stepper_3 (.ADVANCE(and_5_out), .CLK(CLK), .RST(RST), .VALUE(NUM_PASS), .HALT(halt));
  STEPPER stepper_4 (.ADVANCE(and_6_out), .CLK(CLK), .RST(RST), .VALUE(NUM_FAIL), .HALT(halt));
  Adder #(.width(24)) adder_1 (.a(NUM_FAIL), .b(NUM_PASS), .out(adder_1_out));  // open: cin, cout
  STEPPER stepper_5 (.ADVANCE(1'b1), .CLK(CLK), .RST(RST), .VALUE(stepper_5_value), .HALT(halt));
  TRIGGER trigger_1 (.INPUT(adder_1_out), .TRIGGER(24'h5f), .CLK(CLK), .RST(RST), .TRIGGERED(DONE));
  TRIGGER trigger_2 (.INPUT(stepper_5_value), .TRIGGER(24'h251c), .CLK(CLK), .RST(RST), .TRIGGERED(TIMEOUT));
  or or_1 (halt, DONE, TIMEOUT);

  // Notes on the sheet:
  //   Test Inputs
  //   contents of rom_1 (hex, n*v repeats v):
  //   0 1 0 1 1 0 1 0 1 1 0 0 0 1 1 0 0 1 1 0 1 0 1 1 1 0 1 0 0 1 0 1 1 0 1 0 1 1 5*0 1 1 1 0 1 0 1 0 0 1
  //   1 0 1 1 4*0 1 0 1 1 0 1 0 1 1 6*0 1 1 0 1 0 1 0 1 0 1 1 0 1 1 0 1 0 8*1 0 1 0 1 0 1 0 0 0 1 0 1 1 0
  //   4*1 0 1 0 1 1 1 4*0 1 0 4*1 0 0 0 1 0 1 0 0 0 1 1 0 1 1 0 1 0 1 0 1 1 0 1 0 1 1 0 1 0 1 1 1 0 1 1 1
  //   0 1 1 0 1 1 0 1 0 1 0 0 0 1 0 1 4*0 4*1 0 0 1 5*0 1 1 0 1 0 4*1 0 0 1 1 0 1 0 1 0 1 0 6*1 0 0 0 1 1
  //   1 0 1 0 1 0 1 1 0 1 1 5*0 5*1 0 1 0 1 1 1 0 1 1 0 1 1 0 1 0 1 1 0 0 1 0 1 1 0 1 0 1 1 0 0 0 1 0 0 1
  //   0 1 1 0 1 0 0 0 1 1 0 1 0 1 0 0 1 1 0 1 1 1 0 1 1 0 1 0 1 0 0 1 1 0 4*1 0 1 0 1 7*0 1 1 1 0 1 0 5*1
  //   0 1 1 0 0 1 0 1 0 1 1 0 0 1 1 0 1 0 1 0 1 1 0 5*1 0 1 0 1 0 0 0 1 1 1 0 1 0 1 1 0 1 0 1 1 0 0 0 5*1
  //   0 1 0 1 0 1 1 0 1 1 4*0 1 0 0 4*1 0 1 0 1 0 0 1 1 0 1 0 1 1 0 1 0 1 0 1 1 0 1 1 0 1 1 1 0 1 0 1 0 1
  //   1 0 1 1 0 0 0 1 0 1 0 1 1 0 1 0 5*1 0 1 0 1 0 0 5*1 0 1 0 1 0 1 1 0 1 1 0 0 4*1 0 1 0 1 0 1 1 0 1 1
  //   6*0 1 1 0 1 0 1 0 1 1 0 1 1 5*0 1 1 0 1 1 0 1 0 4*1 0 1 0 1 0 0 1 0 6*1 0 1 0 1 0 0 0 1 1 0 1 0 1 0
  //   0 1 1 1 4*0 1 1 0 1 0 1 0 1 0 1 1 1 0 1 1 0 4*1 0 1 0 1 0 0 1 1 0 1 1 0 1 0 1 4*0 1 0 1 1 0 1 0 1 1
  //   4*0 1 0 0 1 0 1 1 0 1 0 0 1 1 1 0 1 0 1 0 1 1 6*0 1 0 1 0 1 0 1 0 0 0 1 1 1 0 1 0 1 1 0 1 0 1 0 1 0
  //   0 0 1 0 0 0 1 0 1 1 0 1 0 1 1 4*0 1 1 1 0 0 6*1 0 1 0 1 1 0 1 0 1 1 0 0 0 1 1 0 1 1 1 5*0 1 0 1 1 0
  //   1 0 1 1 0 1 0 1 1 0 1 0 1 0 1 1 0 1 0 1 1 0 0 5*1 0 0 1 0 1 1 0 1 0 1 1 0 0 0 1 1 0 1 4*0 1 0 1 1 0
  //   1 0 1 0 0 1 1 0 1 1 0 0 1 1 1 0 1 0 1 0 0 1 0 1 1 0 1 0 1 0 1 1 0 1 1 0 0 1 0 1 1 0 1 0 1 0 1 0 1 0
  //   0 1 0 1 1 0 1 0 1 1 0 0 0 1 1 0 1 0 4*1 0 1 1 0 0 0 4*1 0 1 0 1 4*0 1 1 0 1 0 0 0 1 1 1 0 1 1 1 0 0
  //   0 1 1 0 1 0 1 0 1 1 0 0 1 1 1 0 1 0 1 0 0 1 1 0 0 1 1 0 1 0 1 0 1 1 0 1 1 5*0 1 0 0 1 0 1 0 1 1 0 1
  //   0 1 1 1 0 0 1 1 1 0 1 0 1 0 0 1 1 0 7*1 0 1 0 1 0 1 1 1
  //   Randomly offer/accept data
  //   Expected Outputs
  //   contents of rom_2 (hex, n*v repeats v):
  //   3a 49 5c 3d 5b 59 4c 53 71 43 79 6a 77 57 4a 7d 4b 38 62 68 4f 51 34 27 55 78 2b 4d 2c 25 39 33 4e
  //   74 7a 5a 40 26 5d 6f 5f 23 5e 46 47 3f 3c 7c 50 30 32 56 67 35 58 31 2f 63 29 54 21 70 6c 66 42 76
  //   60 65 69 28 37 61 2d 24 73 7b 72 7e 45 3b 48 22 6e 36 52 6b 6d 75 2e 2a 3e 64 44 20 41
  //   # Tests:
  //   Timeout:
endmodule

module HUFFDEC (
  input  X,
  input  RDY_IN,
  input  VAL_IN,
  input  CLK,
  input  RST,
  output [7:0] CHAR,
  output VAL_OUT,
  output RDY_OUT
);

  wire and_1_out, and_2_out, or_1_out, or_2_out;
  wire [7:0] multiplexer_1_out, multiplexer_2_out, register_1_q;
  wire [15:8] rom_1_data;

  not not_1 (RDY_OUT, VAL_OUT);
  or or_1 (or_1_out, X, VAL_OUT);
  Multiplexer #(.width(8), .enable("false")) multiplexer_1 (
    .in0(rom_1_data), .in1(CHAR), .out(multiplexer_1_out), .sel(or_1_out));
  and and_1 (and_1_out, VAL_IN, ~VAL_OUT);  // AND_Gate
  and and_2 (and_2_out, VAL_OUT, RDY_IN);
  Multiplexer #(.width(8), .enable("false")) multiplexer_2 (
    .in0(multiplexer_1_out), .in1({8{1'b0}}), .out(multiplexer_2_out), .sel(VAL_OUT));
  or or_2 (or_2_out, and_1_out, and_2_out);
  Register register_1 (.D(multiplexer_2_out), .en(or_2_out), .Q(register_1_q), .clk(CLK), .clr(RST));
  ROM #(.dataWidth(17)) rom_1 (.addr(register_1_q), .data({VAL_OUT, rom_1_data, CHAR}));  // open: sel

  // Notes on the sheet:
  //   Tree ROM
  //   contents of rom_1 (hex, n*v repeats v):
  //   bbbc 10020 10024 10028 1002c 10030 10034 10038 1003c 10040 10044 10048 1004c 10050 10054 10058 1005c
  //   10060 10064 10068 1006c 10070 10074 10078 1007c 10023 10027 1002b 1002f 10033 10037 1003b 1003f
  //   10043 10047 1004b 1004f 10053 10057 1005b 1005f 10063 10067 1006b 1006f 10073 10077 1007b 10022
  //   10026 1002a 1002e 10032 10036 1003a 1003e 10042 10046 1004a 1004e 10052 10056 1005a 1005e 10062
  //   10066 1006a 1006e 10072 10076 1007a 1007e 10021 10025 10029 1002d 10031 10035 10039 1003d 10041
  //   10045 10049 1004d 10051 10055 10059 1005d 10061 10065 10069 1006d 10071 10075 10079 1007d 181a 2f30
  //   3760 6103 862 3663 6457 2710 4a11 6531 4f47 4901 663f 1f20 6768 1b69 6a1c 46b 6c6d 6e6f 7071 7219
  //   7302 2874 f54 753e 764b 3d09 3277 5678 4833 2679 553a 7a39 237b 7c22 b7d 7e7f 210a 5280 240d 3b0c
  //   530e 3881 3c82 5183 2584 8550 8687 8889 8a8b 8c8d 8e8f 9091 925c 9394 1795 4696 4542 9798 2e41 995e
  //   1e07 9a35 4e2a 4d06 2b9b 5d40 131d 159c 2905 129d 5b34 9e9f a014 a116 a24c a343 2d5a a4a5 442c a6a7
  //   5fa8 a959 aa58 abac adae afb0 b1b2 b3b4 b5b6 b7b8 b9ba
endmodule
