// Logisim project lib3827.circ as structural Verilog: 3 circuits, main circuit STEPPER
module STEPPER (
  input  HALT,
  input  ADVANCE,
  input  CLK,
  input  RST,
  output [23:0] VALUE
);

  wire and_1_out;

  and and_1 (and_1_out, ~HALT, ADVANCE);  // AND_Gate
  Counter #(.width(24), .max('hffffff), .ongoal("stay")) counter_1 (
    .count(and_1_out), .Q(VALUE), .clk(CLK), .clr(RST));  // open: load, D, carry
endmodule

module TRIGGER (
  input  CLK,
  input  RST,
  input  [23:0] INPUT,
  input  [23:0] TRIGGER,
  output TRIGGERED
);

  wire comparator_1_eq, register_1_q;

  Comparator #(.width(24)) comparator_1 (.a(INPUT), .b(TRIGGER), .eq(comparator_1_eq));  // open: gt, lt
  Register #(.width(1)) register_1 (.D(TRIGGERED), .Q(register_1_q), .clk(CLK), .clr(RST));  // open: en
  or or_1 (TRIGGERED, register_1_q, comparator_1_eq);
endmodule

module LIBUF (
  input  [15:0] DATA,
  input  VAL,
  input  RDY,
  input  CLK,
  input  RST,
  output [15:0] DATA_2,
  output VAL_2,
  output RDY_2
);

  wire and_1_out, and_2_out, or_1_out;
  wire [16:0] multiplexer_1_out, multiplexer_2_out, multiplexer_3_out, multiplexer_4_out, register_1_q;

  not not_1 (RDY_2, register_1_q[16]);
  Multiplexer #(.width(17), .enable("false")) multiplexer_1 (
    .in0(register_1_q), .in1({VAL, DATA}), .out(multiplexer_1_out), .sel(and_1_out));
  and and_1 (and_1_out, ~or_1_out, ~register_1_q[16]);  // AND_Gate
  Multiplexer #(.width(17), .enable("false")) multiplexer_2 (
    .in0(multiplexer_1_out), .in1({17{1'b0}}), .out(multiplexer_2_out), .sel(and_2_out));
  and and_2 (and_2_out, or_1_out, register_1_q[16]);
  Multiplexer #(.width(17), .enable("false")) multiplexer_3 (
    .in0({VAL, DATA}), .in1(register_1_q), .out(multiplexer_3_out), .sel(register_1_q[16]));
  Register #(.width(17)) register_1 (.D(multiplexer_2_out), .Q(register_1_q), .clk(CLK), .clr(RST));  // open: en
  Multiplexer #(.width(17), .enable("false")) multiplexer_4 (
    .in0({VAL_2, DATA_2}), .in1(multiplexer_3_out), .out(multiplexer_4_out), .sel(or_1_out));
  Register #(.width(17)) register_2 (.D(multiplexer_4_out), .Q({VAL_2, DATA_2}), .clk(CLK), .clr(RST));  // open: en
  or or_1 (or_1_out, ~VAL_2, RDY);  // OR_Gate

  // Notes on the sheet:
  //   <-- Input buffer
  //   Output buffer -->
endmodule
