// Logisim project scaffolding-msm2243.circ as structural Verilog: 5 circuits, main circuit PIPE_KEYVAL
// HALT
module main (
  input  in_1,
  input  in_2,
  output [23:0] NUM_PASS,
  output [23:0] NUM_FAIL,
  output DONE,
  output TIMEOUT,
  output [23:0] NUM_CYCLES,
  output halt
);

  wire and_2_out, and_3_out, and_5_out, and_6_out, CLK, comparator_1_lt, comparator_2_eq, \input , or_1_out,
       \output , pipe_keyval_1_cmd_rdy, pipe_keyval_1_res_val, pipe_keyval_1_slow_cmd_val,
       pipe_keyval_1_slow_res_rdy, RST, slow_keyval_1_cmd_rdy, slow_keyval_1_res_val, t_ff_1_qn;
  wire [1:0] multiplexer_1_out, random_1_out;
  wire [16:0] pipe_keyval_1_res, pipe_keyval_1_slow_cmd, rom_1_data, rom_2_data, slow_keyval_1_res;
  wire [23:0] adder_1_out, stepper_1_value, stepper_2_value;

  Clock clock_1 (.out(CLK));
  Button button_1 (.out(RST));
  STEPPER stepper_1 (.ADVANCE(\input ), .CLK(CLK), .RST(RST), .VALUE(stepper_1_value), .HALT(halt));
  Comparator #(.width(24)) comparator_1 (.a(stepper_1_value), .b(24'h64), .lt(comparator_1_lt));  // open: gt, eq
  ROM #(.addrWidth(24), .dataWidth(17)) rom_1 (.addr(stepper_1_value), .data(rom_1_data));  // open: sel
  and and_1 (\input , and_2_out, pipe_keyval_1_cmd_rdy);
  T_Flip_Flop t_ff_1 (.clk(CLK), .T(or_1_out), .Qn(t_ff_1_qn), .reset(RST), .en(in_2));  // open: Q, preset
  or or_1 (or_1_out, \input , \output );
  and and_2 (and_2_out, ~halt, t_ff_1_qn, comparator_1_lt, multiplexer_1_out[1]);  // AND_Gate
  Random #(.width(2), .seed(1234)) random_1 (.clk(CLK), .out(random_1_out), .clr(RST));  // open: next
  PIPE_KEYVAL pipe_keyval_1 (
    .CLK(CLK), .RST(RST), .CMD(rom_1_data), .CMD_VAL(and_2_out), .CMD_RDY(pipe_keyval_1_cmd_rdy),
    .SLOW_CMD(pipe_keyval_1_slow_cmd), .SLOW_CMD_VAL(pipe_keyval_1_slow_cmd_val),
    .SLOW_RES(slow_keyval_1_res), .RES(pipe_keyval_1_res), .SLOW_RES_VAL(slow_keyval_1_res_val),
    .RES_VAL(pipe_keyval_1_res_val), .SLOW_RES_RDY(pipe_keyval_1_slow_res_rdy), .RES_RDY(and_3_out),
    .SLOW_CMD_RDY(slow_keyval_1_cmd_rdy));
  SLOW_KEYVAL slow_keyval_1 (
    .CMD(pipe_keyval_1_slow_cmd), .CMD_RDY(slow_keyval_1_cmd_rdy), .CMD_VAL(pipe_keyval_1_slow_cmd_val),
    .RES_RDY(pipe_keyval_1_slow_res_rdy), .RES_VAL(slow_keyval_1_res_val), .RES(slow_keyval_1_res),
    .CLK(CLK), .RST(RST));
  Multiplexer #(.width(2), .enable("false")) multiplexer_1 (
    .in0(random_1_out), .in1(2'b11), .out(multiplexer_1_out), .sel(in_1));
  and and_3 (and_3_out, multiplexer_1_out[0], ~halt);  // AND_Gate
  and and_4 (\output , pipe_keyval_1_res_val, and_3_out);
  STEPPER stepper_2 (.ADVANCE(\output ), .CLK(CLK), .RST(RST), .VALUE(stepper_2_value), .HALT(halt));
  ROM #(.addrWidth(24), .dataWidth(17)) rom_2 (.addr(stepper_2_value), .data(rom_2_data));  // open: sel
  Comparator #(.width(17)) comparator_2 (.a(pipe_keyval_1_res), .b(rom_2_data), .eq(comparator_2_eq));  // open: gt, lt
  and and_5 (and_5_out, \output , comparator_2_eq);
  and and_6 (and_6_out, ~comparator_2_eq, \output );  // AND_Gate
  STEPPER stepper_3 (.ADVANCE(and_5_out), .CLK(CLK), .RST(RST), .VALUE(NUM_PASS), .HALT(halt));
  STEPPER stepper_4 (.ADVANCE(and_6_out), .CLK(CLK), .RST(RST), .VALUE(NUM_FAIL), .HALT(halt));
  STEPPER stepper_5 (.ADVANCE(1'b1), .CLK(CLK), .RST(RST), .VALUE(NUM_CYCLES), .HALT(halt));
  // Probe on NUM_PASS
  // Probe on NUM_FAIL
  // Probe on NUM_CYCLES
  Adder #(.width(24)) adder_1 (.a(NUM_FAIL), .b(NUM_PASS), .out(adder_1_out));  // open: cin, cout
  TRIGGER trigger_1 (.INPUT(adder_1_out), .TRIGGER(24'h64), .CLK(CLK), .RST(RST), .TRIGGERED(DONE));
  TRIGGER trigger_2 (.INPUT(NUM_CYCLES), .TRIGGER(24'h2710), .CLK(CLK), .RST(RST), .TRIGGERED(TIMEOUT));
  or or_2 (halt, DONE, TIMEOUT);

  // Other names for the same wires on the sheet: latency_mode = in_2; perf_mode = in_1

  // Notes on the sheet:
  //   Test Inputs
  //   contents of rom_1 (hex, n*v repeats v):
  //   17f41 7d73 7f07 7e6e 80b8 17ff1 7f8a 7f61 17e38 7f7e 17f75 7f05 7d2f 7edc 17eb6 806c 7e96 7ed8 7e3e
  //   7e6a 17dac 7e70 7f64 7d07 17e97 7c2b 808a 7e3b 8075 7e8c 80d2 7fbd 7d6d 17ede 7f7c 8058 7e75 17e3a
  //   17dcc 7dd1 7f15 17d03 7f9f 7f11 17e45 7e74 7e62 7f30 17f35 7ed1 17fb8 17fb4 7ef9 7e84 17e93 7ea1
  //   17ee0 81db 806a 7e02 80f6 7f2b 8082 7e58 17e31 17eaa 7edf 7f04 17dc8 8136 8058 7daf 7fb9 17e2b 7f99
  //   805e 7e9a 80e3 17e0a 17edd 7f9d 7e60 7f44 7f90 7ec9 7f03 7fe2 17f3d 7e2a 17fbe 17ff8 7e4b 7ea6 17f02
  //   7e73 8010 811c 17e9e 7da9 7e8a
  //   Expected Outputs
  //   contents of rom_2 (hex, n*v repeats v):
  //   17f41 7d00 7f41 7e00 8000 17ff1 7ff1 7ff1 17e38 7ff1 17f75 7f75 7d00 7e38 17eb6 8000 4*7eb6 17dac
  //   7eb6 7f75 7dac 17e97 7c00 8000 7e97 8000 7e97 8000 7f75 7dac 17ede 7f75 8000 7ede 17e3a 17dcc 7dcc
  //   7f75 17d03 7f75 7f75 17e45 7e45 7e45 7f75 17f35 7e45 17fb8 17fb4 7e45 7e45 17e93 7e93 17ee0 8100
  //   8000 7ee0 8000 7fb4 8000 7ee0 17e31 17eaa 7eaa 7fb4 17dc8 8100 8000 7dc8 7fb4 17e2b 7fb4 8000 7e2b
  //   8000 17e0a 17edd 7fb4 7edd 7fb4 7fb4 7edd 7fb4 7fb4 17f3d 7edd 17fbe 17ff8 7edd 7edd 17f02 7edd 8000
  //   8100 17e9e 7dc8 7e9e
endmodule

module PIPE_KEYVAL (
  input  [16:0] CMD,
  input  CMD_VAL,
  input  [16:0] SLOW_RES,
  input  CLK,
  input  RST,
  input  SLOW_CMD_RDY,
  input  SLOW_RES_VAL,
  input  RES_RDY,
  output [16:0] SLOW_CMD,
  output [16:0] RES,
  output CMD_RDY,
  output SLOW_CMD_VAL,
  output RES_VAL,
  output SLOW_RES_RDY
);

  wire and_3_out, INFLOW, not_1_out, OUTFLOW, stage_1_op_out, stage_1_slow_out, stage_1_val_out,
       stage_2_en_out, stage_2_op_out, stage_2_slow_out, stage_2_val_out, stage_3_en_out, stage_3_op_out,
       stage_3_slow_out, stage_3_val_out, stage_4_en_out, stage_4_op_out, stage_4_slow_out, stage_4_val_out,
       stage_5_en_out, stage_5_op_out, stage_5_slow_out, stage_5_val_out, stage_6_en_out, stage_6_op_out,
       stage_6_slow_out, stage_6_val_out, stage_7_en_out, stage_7_op_out, stage_7_slow_out, stage_7_val_out,
       stage_8_en_out, stage_8_op_out, stage_8_slow_out, stage_8_val_out, stage_9_en_out, stage_9_op_out,
       stage_9_slow_out, stage_9_val_out, stage_10_en_out, stage_10_op_out, stage_10_slow_out,
       stage_10_val_out, stage_11_en_out, stage_11_op_out, stage_11_slow_out, stage_11_val_out,
       stage_12_en_out, stage_12_slow_out, stage_12_val_out;
  wire [7:0] stage_1_ad_out, stage_1_va_out, stage_2_ad_out, stage_2_va_out, stage_3_ad_out, stage_3_va_out,
       stage_4_ad_out, stage_4_va_out, stage_5_ad_out, stage_5_va_out, stage_6_ad_out, stage_6_va_out,
       stage_7_ad_out, stage_7_va_out, stage_8_ad_out, stage_8_va_out, stage_9_ad_out, stage_9_va_out,
       stage_10_ad_out, stage_10_va_out, stage_11_ad_out, stage_11_va_out;

  STAGE stage_1 (
    .VAL_IN(CMD_VAL), .ACTIVE_IN(CMD_VAL), .OP_IN(CMD[16]), .AD_IN(CMD[15:8]), .VA_IN(CMD[7:0]),
    .O_VA(RES[7:0]), .CMD_K(CMD[15:8]), .O_K(RES[15:8]), .VAL_OUT(stage_1_val_out),
    .SLOW_OUT(stage_1_slow_out), .OP_OUT(stage_1_op_out), .AD_OUT(stage_1_ad_out), .VA_OUT(stage_1_va_out),
    .IN(INFLOW), .EN_IN(stage_2_en_out), .OUT(OUTFLOW), .CLK(CLK), .RST(RST), .COP(CMD[16]), .EN_OUT(CMD_RDY));
  and and_1 (INFLOW, CMD_VAL, CMD_RDY);
  STAGE stage_2 (
    .VAL_IN(stage_1_val_out), .ACTIVE_IN(stage_1_slow_out), .OP_IN(stage_1_op_out), .AD_IN(stage_1_ad_out),
    .VA_IN(stage_1_va_out), .O_VA(RES[7:0]), .CMD_K(CMD[15:8]), .O_K(RES[15:8]), .VAL_OUT(stage_2_val_out),
    .SLOW_OUT(stage_2_slow_out), .OP_OUT(stage_2_op_out), .AD_OUT(stage_2_ad_out), .VA_OUT(stage_2_va_out),
    .IN(INFLOW), .EN_IN(stage_3_en_out), .OUT(OUTFLOW), .CLK(CLK), .RST(RST), .COP(CMD[16]),
    .EN_OUT(stage_2_en_out));
  STAGE stage_3 (
    .VAL_IN(stage_2_val_out), .ACTIVE_IN(stage_2_slow_out), .OP_IN(stage_2_op_out), .AD_IN(stage_2_ad_out),
    .VA_IN(stage_2_va_out), .O_VA(RES[7:0]), .CMD_K(CMD[15:8]), .O_K(RES[15:8]), .VAL_OUT(stage_3_val_out),
    .SLOW_OUT(stage_3_slow_out), .OP_OUT(stage_3_op_out), .AD_OUT(stage_3_ad_out), .VA_OUT(stage_3_va_out),
    .IN(INFLOW), .EN_IN(stage_4_en_out), .OUT(OUTFLOW), .CLK(CLK), .RST(RST), .COP(CMD[16]),
    .EN_OUT(stage_3_en_out));
  STAGE stage_4 (
    .VAL_IN(stage_3_val_out), .ACTIVE_IN(stage_3_slow_out), .OP_IN(stage_3_op_out), .AD_IN(stage_3_ad_out),
    .VA_IN(stage_3_va_out), .O_VA(RES[7:0]), .CMD_K(CMD[15:8]), .O_K(RES[15:8]), .VAL_OUT(stage_4_val_out),
    .SLOW_OUT(stage_4_slow_out), .OP_OUT(stage_4_op_out), .AD_OUT(stage_4_ad_out), .VA_OUT(stage_4_va_out),
    .IN(INFLOW), .EN_IN(stage_5_en_out), .OUT(OUTFLOW), .CLK(CLK), .RST(RST), .COP(CMD[16]),
    .EN_OUT(stage_4_en_out));
  STAGE stage_5 (
    .VAL_IN(stage_4_val_out), .ACTIVE_IN(stage_4_slow_out), .OP_IN(stage_4_op_out), .AD_IN(stage_4_ad_out),
    .VA_IN(stage_4_va_out), .O_VA(RES[7:0]), .CMD_K(CMD[15:8]), .O_K(RES[15:8]), .VAL_OUT(stage_5_val_out),
    .SLOW_OUT(stage_5_slow_out), .OP_OUT(stage_5_op_out), .AD_OUT(stage_5_ad_out), .VA_OUT(stage_5_va_out),
    .IN(INFLOW), .EN_IN(stage_6_en_out), .OUT(OUTFLOW), .CLK(CLK), .RST(RST), .COP(CMD[16]),
    .EN_OUT(stage_5_en_out));
  STAGE stage_6 (
    .VAL_IN(stage_5_val_out), .ACTIVE_IN(stage_5_slow_out), .OP_IN(stage_5_op_out), .AD_IN(stage_5_ad_out),
    .VA_IN(stage_5_va_out), .O_VA(RES[7:0]), .CMD_K(CMD[15:8]), .O_K(RES[15:8]), .VAL_OUT(stage_6_val_out),
    .SLOW_OUT(stage_6_slow_out), .OP_OUT(stage_6_op_out), .AD_OUT(stage_6_ad_out), .VA_OUT(stage_6_va_out),
    .IN(INFLOW), .EN_IN(stage_7_en_out), .OUT(OUTFLOW), .CLK(CLK), .RST(RST), .COP(CMD[16]),
    .EN_OUT(stage_6_en_out));
  STAGE stage_7 (
    .VAL_IN(stage_6_val_out), .ACTIVE_IN(stage_6_slow_out), .OP_IN(stage_6_op_out), .AD_IN(stage_6_ad_out),
    .VA_IN(stage_6_va_out), .O_VA(RES[7:0]), .CMD_K(CMD[15:8]), .O_K(RES[15:8]), .VAL_OUT(stage_7_val_out),
    .SLOW_OUT(stage_7_slow_out), .OP_OUT(stage_7_op_out), .AD_OUT(stage_7_ad_out), .VA_OUT(stage_7_va_out),
    .IN(INFLOW), .EN_IN(stage_8_en_out), .OUT(OUTFLOW), .CLK(CLK), .RST(RST), .COP(CMD[16]),
    .EN_OUT(stage_7_en_out));
  STAGE stage_8 (
    .VAL_IN(stage_7_val_out), .ACTIVE_IN(stage_7_slow_out), .OP_IN(stage_7_op_out), .AD_IN(stage_7_ad_out),
    .VA_IN(stage_7_va_out), .O_VA(RES[7:0]), .CMD_K(CMD[15:8]), .O_K(RES[15:8]), .VAL_OUT(stage_8_val_out),
    .SLOW_OUT(stage_8_slow_out), .OP_OUT(stage_8_op_out), .AD_OUT(stage_8_ad_out), .VA_OUT(stage_8_va_out),
    .IN(INFLOW), .EN_IN(stage_9_en_out), .OUT(OUTFLOW), .CLK(CLK), .RST(RST), .COP(CMD[16]),
    .EN_OUT(stage_8_en_out));
  STAGE stage_9 (
    .VAL_IN(stage_8_val_out), .ACTIVE_IN(stage_8_slow_out), .OP_IN(stage_8_op_out), .AD_IN(stage_8_ad_out),
    .VA_IN(stage_8_va_out), .O_VA(RES[7:0]), .CMD_K(CMD[15:8]), .O_K(RES[15:8]), .VAL_OUT(stage_9_val_out),
    .SLOW_OUT(stage_9_slow_out), .OP_OUT(stage_9_op_out), .AD_OUT(stage_9_ad_out), .VA_OUT(stage_9_va_out),
    .IN(INFLOW), .EN_IN(stage_10_en_out), .OUT(OUTFLOW), .CLK(CLK), .RST(RST), .COP(CMD[16]),
    .EN_OUT(stage_9_en_out));
  STAGE stage_10 (
    .VAL_IN(stage_9_val_out), .ACTIVE_IN(stage_9_slow_out), .OP_IN(stage_9_op_out), .AD_IN(stage_9_ad_out),
    .VA_IN(stage_9_va_out), .O_VA(RES[7:0]), .CMD_K(CMD[15:8]), .O_K(RES[15:8]), .VAL_OUT(stage_10_val_out),
    .SLOW_OUT(stage_10_slow_out), .OP_OUT(stage_10_op_out), .AD_OUT(stage_10_ad_out),
    .VA_OUT(stage_10_va_out), .IN(INFLOW), .EN_IN(stage_11_en_out), .OUT(OUTFLOW), .CLK(CLK), .RST(RST),
    .COP(CMD[16]), .EN_OUT(stage_10_en_out));
  STAGE stage_11 (
    .VAL_IN(stage_10_val_out), .ACTIVE_IN(stage_10_slow_out), .OP_IN(stage_10_op_out),
    .AD_IN(stage_10_ad_out), .VA_IN(stage_10_va_out), .O_VA(RES[7:0]), .CMD_K(CMD[15:8]), .O_K(RES[15:8]),
    .VAL_OUT(stage_11_val_out), .SLOW_OUT(stage_11_slow_out), .OP_OUT(stage_11_op_out),
    .AD_OUT(stage_11_ad_out), .VA_OUT(stage_11_va_out), .IN(INFLOW), .EN_IN(stage_12_en_out), .OUT(OUTFLOW),
    .CLK(CLK), .RST(RST), .COP(CMD[16]), .EN_OUT(stage_11_en_out));
  STAGE stage_12 (
    .VAL_IN(stage_11_val_out), .ACTIVE_IN(stage_11_slow_out), .OP_IN(stage_11_op_out),
    .AD_IN(stage_11_ad_out), .VA_IN(stage_11_va_out), .O_VA(RES[7:0]), .CMD_K(CMD[15:8]), .O_K(RES[15:8]),
    .VAL_OUT(stage_12_val_out), .SLOW_OUT(stage_12_slow_out), .OP_OUT(SLOW_CMD[16]), .AD_OUT(SLOW_CMD[15:8]),
    .VA_OUT(SLOW_CMD[7:0]), .IN(1'b0), .EN_IN(OUTFLOW), .OUT(1'b0), .CLK(CLK), .RST(RST), .COP(CMD[16]),
    .EN_OUT(stage_12_en_out));
  Multiplexer #(.width(17), .enable("false")) multiplexer_1 (
    .in0(SLOW_CMD), .in1(SLOW_RES), .out(RES), .sel(SLOW_RES_VAL));
  and and_2 (SLOW_CMD_VAL, stage_12_val_out, stage_12_slow_out);
  not not_1 (not_1_out, stage_12_slow_out);
  and and_3 (and_3_out, not_1_out, stage_12_val_out, SLOW_CMD_RDY, RES_RDY);
  or or_1 (RES_VAL, and_3_out, SLOW_RES_VAL);
  and and_4 (OUTFLOW, RES_RDY, RES_VAL);

  assign SLOW_RES_RDY = RES_RDY;

  // Other names for the same wires on the sheet: O_VA[7:0] = RES[7:0]; O_K[7:0] = RES[15:8]
endmodule

module SLOW_KEYVAL (
  input  [16:0] CMD,
  input  CLK,
  input  RST,
  input  RES_RDY,
  input  CMD_VAL,
  output [16:0] RES,
  output CMD_RDY,
  output RES_VAL
);

  wire and_1_out, comparator_1_eq, slow_keyval_cntl_1_accept;
  wire [3:0] counter_1_q;
  wire [7:0] register_1_q;

  Counter #(.width(4), .max('hf)) counter_1 (
    .Q(counter_1_q), .clk(CLK), .clr(slow_keyval_cntl_1_accept));  // open: load, D, count, carry
  Comparator #(.width(4)) comparator_1 (.a(4'b0110), .b(counter_1_q), .eq(comparator_1_eq));  // open: gt, lt
  SLOW_KEYVAL_CNTL slow_keyval_cntl_1 (
    .CLK(CLK), .RST(RST), .RES_RDY(RES_RDY), .DONE(comparator_1_eq), .CMD_VAL(CMD_VAL), .READY(CMD_RDY),
    .ACCEPT(slow_keyval_cntl_1_accept), .OFFER(RES_VAL));  // open: PROCESS
  Register #(.width(17)) register_1 (.D(CMD), .en(CMD_RDY), .Q({RES[16:8], register_1_q}), .clk(CLK), .clr(RST));
  and and_1 (and_1_out, RES[16], slow_keyval_cntl_1_accept);
  RAM #(.bus("separate")) ram_1 (
    .addr(RES[15:8]), .din(register_1_q), .data(RES[7:0]), .str(and_1_out), .clk(CLK), .ld(1'b1), .clr(RST));  // open: sel
endmodule

module SLOW_KEYVAL_CNTL (
  input  CLK,
  input  RST,
  input  RES_RDY,
  input  DONE,
  input  CMD_VAL,
  output READY,
  output ACCEPT,
  output PROCESS,
  output OFFER
);

  wire and_1_out, and_2_out, and_3_out;
  wire [1:0] d0_out, register_1_q;

  Register #(.width(2)) register_1 (.D(d0_out), .Q(register_1_q), .clk(CLK), .clr(RST));  // open: en
  Decoder #(.select(2), .disabled(0), .enable("false")) decoder_1 (
    .out0(READY), .out1(ACCEPT), .out2(PROCESS), .out3(OFFER), .sel(register_1_q));
  or d1 (d0_out[1], ACCEPT, PROCESS, and_1_out);
  and and_1 (and_1_out, ~RES_RDY, OFFER);  // AND_Gate
  and and_2 (and_2_out, DONE, PROCESS);
  or d0 (d0_out[0], and_1_out, and_2_out, and_3_out);
  and and_3 (and_3_out, CMD_VAL, READY);
endmodule

// BEAUTIFUL
module STAGE (
  input  CLK,
  input  VAL_IN,
  input  RST,
  input  EN_IN,
  input  [7:0] O_K,
  input  ACTIVE_IN,
  input  OUT,
  input  IN,
  input  COP,
  input  [7:0] CMD_K,
  input  OP_IN,
  input  [7:0] AD_IN,
  input  [7:0] VA_IN,
  input  [7:0] O_VA,
  output VAL_OUT,
  output EN_OUT,
  output SLOW_OUT,
  output OP_OUT,
  output [7:0] AD_OUT,
  output [7:0] VA_OUT
);

  wire comparator_1_eq, comparator_2_eq, d_ff_2_q, not_1_out, RD, WRT;
  wire [7:0] register_2_q;

  D_Flip_Flop d_ff_1 (.clk(CLK), .D(VAL_IN), .Q(VAL_OUT), .en(EN_OUT), .reset(RST));  // open: Qn, preset
  not not_1 (not_1_out, VAL_OUT);
  or or_1 (EN_OUT, not_1_out, EN_IN);
  D_Flip_Flop d_ff_2 (.clk(CLK), .D(ACTIVE_IN), .Q(d_ff_2_q), .en(EN_OUT), .reset(RST));  // open: Qn, preset
  D_Flip_Flop d_ff_3 (.clk(CLK), .D(OP_IN), .Q(OP_OUT), .en(EN_OUT), .reset(RST));  // open: Qn, preset
  Register register_1 (.D(AD_IN), .en(EN_OUT), .Q(AD_OUT), .clk(CLK), .clr(RST));
  Register register_2 (.D(VA_IN), .en(EN_OUT), .Q(register_2_q), .clk(CLK), .clr(RST));
  and and_1 (SLOW_OUT, d_ff_2_q, ~WRT, ~RD);  // AND_Gate
  Multiplexer #(.width(8), .enable("false")) multiplexer_1 (.in0(register_2_q), .in1(O_VA), .out(VA_OUT), .sel(RD));
  Comparator comparator_1 (.a(O_K), .b(AD_OUT), .eq(comparator_1_eq));  // open: gt, lt
  Comparator comparator_2 (.a(CMD_K), .b(AD_OUT), .eq(comparator_2_eq));  // open: gt, lt
  and and_2 (RD, ~OP_OUT, comparator_1_eq, OUT);  // AND_Gate
  and and_3 (WRT, IN, COP, comparator_2_eq, OP_OUT);

  // Other names for the same wires on the sheet: AD[7:0] = AD_OUT; C = OP_OUT; EN = EN_OUT
endmodule
