// Logisim project scaffolding.circ as structural Verilog: 5 circuits, main circuit main
// HALT
module main (
  input  in_1,
  output [23:0] NUM_PASS,
  output [23:0] NUM_FAIL,
  output DONE,
  output TIMEOUT,
  output [23:0] NUM_CYCLES,
  output halt
);

  wire and_2_out, and_3_out, and_5_out, and_6_out, CLK, comparator_1_lt, comparator_2_eq, huffdec_1_addr_val,
       huffdec_1_char_val, huffdec_1_data_rdy, huffdec_1_x_rdy, \input , \output , rom_1_data, RST,
       slow_tree_rom_1_addr_rdy, slow_tree_rom_1_data_val;
  wire [1:0] multiplexer_1_out, random_1_out;
  wire [7:0] huffdec_1_addr, huffdec_1_char, rom_2_data;
  wire [16:0] slow_tree_rom_1_data;
  wire [23:0] adder_1_out, stepper_1_value, stepper_2_value;

  Clock clock_1 (.out(CLK));
  Button button_1 (.out(RST));
  STEPPER stepper_1 (.ADVANCE(\input ), .CLK(CLK), .RST(RST), .VALUE(stepper_1_value), .HALT(halt));
  Comparator #(.width(24)) comparator_1 (.a(stepper_1_value), .b(24'h41e), .lt(comparator_1_lt));  // open: gt, eq
  ROM #(.addrWidth(24), .dataWidth(1)) rom_1 (.addr(stepper_1_value), .data(rom_1_data));  // open: sel
  and and_1 (\input , and_2_out, huffdec_1_x_rdy);
  and and_2 (and_2_out, ~halt, comparator_1_lt, multiplexer_1_out[1]);  // AND_Gate
  Random #(.width(2), .seed(1234)) random_1 (.clk(CLK), .out(random_1_out), .clr(RST));  // open: next
  HUFFDEC huffdec_1 (
    .CLK(CLK), .RST(RST), .X(rom_1_data), .DATA(slow_tree_rom_1_data), .X_VAL(and_2_out),
    .DATA_VAL(slow_tree_rom_1_data_val), .X_RDY(huffdec_1_x_rdy), .DATA_RDY(huffdec_1_data_rdy),
    .ADDR(huffdec_1_addr), .ADDR_VAL(huffdec_1_addr_val), .CHAR_VAL(huffdec_1_char_val),
    .ADDR_RDY(slow_tree_rom_1_addr_rdy), .CHAR_RDY(and_3_out), .CHAR(huffdec_1_char));
  SLOW_TREE_ROM slow_tree_rom_1 (
    .ADDR_RDY(slow_tree_rom_1_addr_rdy), .ADDR_VAL(huffdec_1_addr_val), .DATA_RDY(huffdec_1_data_rdy),
    .DATA_VAL(slow_tree_rom_1_data_val), .CLK(CLK), .RST(RST), .ADDR(huffdec_1_addr),
    .DATA(slow_tree_rom_1_data));
  Multiplexer #(.width(2), .enable("false")) multiplexer_1 (
    .in0(random_1_out), .in1(2'b11), .out(multiplexer_1_out), .sel(in_1));
  and and_3 (and_3_out, multiplexer_1_out[0], ~halt);  // AND_Gate
  and and_4 (\output , huffdec_1_char_val, and_3_out);
  STEPPER stepper_2 (.ADVANCE(\output ), .CLK(CLK), .RST(RST), .VALUE(stepper_2_value), .HALT(halt));
  ROM #(.addrWidth(24)) rom_2 (.addr(stepper_2_value), .data(rom_2_data));  // open: sel
  Comparator comparator_2 (.a(huffdec_1_char), .b(rom_2_data), .eq(comparator_2_eq));  // open: gt, lt
  and and_5 (and_5_out, \output , comparator_2_eq);
  and and_6 (and_6_out, ~comparator_2_eq, \output );  // AND_Gate
  STEPPER stepper_3 (.ADVANCE(and_5_out), .CLK(CLK), .RST(RST), .VALUE(NUM_PASS), .HALT(halt));
  STEPPER stepper_4 (.ADVANCE(and_6_out), .CLK(CLK), .RST(RST), .VALUE(NUM_FAIL), .HALT(halt));
  STEPPER stepper_5 (.ADVANCE(1'b1), .CLK(CLK), .RST(RST), .VALUE(NUM_CYCLES), .HALT(halt));
  // Probe on NUM_PASS
  // Probe on NUM_FAIL
  // Probe on NUM_CYCLES
  Adder #(.width(24)) adder_1 (.a(NUM_FAIL), .b(NUM_PASS), .out(adder_1_out));  // open: cin, cout
  TRIGGER trigger_1 (.INPUT(adder_1_out), .TRIGGER(24'h64), .CLK(CLK), .RST(RST), .TRIGGERED(DONE));
  TRIGGER trigger_2 (.INPUT(NUM_CYCLES), .TRIGGER(24'h5258), .CLK(CLK), .RST(RST), .TRIGGERED(TIMEOUT));
  or or_1 (halt, DONE, TIMEOUT);

  // Other names for the same wires on the sheet: perf_mode = in_1

  // Notes on the sheet:
  //   Test Inputs
  //   contents of rom_1 (hex, n*v repeats v):
  //   0 1 1 1 4*0 1 1 0 1 1 0 1 0 1 0 1 1 0 1 1 6*0 1 0 0 0 1 0 1 1 1 0 1 0 1 0 1 1 0 1 1 4*0 1 1 1 0 1 0
  //   1 0 0 0 1 1 0 0 1 0 1 1 0 4*1 0 1 0 1 0 1 1 0 0 1 1 0 1 1 0 1 0 0 0 1 1 0 1 0 5*1 0 1 1 0 1 0 1 0 1
  //   1 0 1 1 1 0 1 0 1 1 0 1 0 5*1 0 1 0 8*1 0 1 0 1 0 0 0 1 0 1 1 0 1 0 4*1 0 0 1 1 0 1 0 1 0 1 1 9*0 1
  //   0 1 1 0 1 0 1 1 0 0 0 1 0 1 0 0 0 1 0 0 1 1 0 1 0 1 0 1 1 0 1 1 0 0 1 0 0 1 0 1 1 0 1 0 1 1 4*0 1 1
  //   0 1 0 5*1 0 1 0 5*1 0 0 1 0 1 0 0 1 0 1 1 0 1 0 1 1 0 0 0 1 1 0 1 1 0 1 0 1 1 0 1 0 1 1 0 0 0 1 0 1
  //   1 0 1 0 1 0 1 0 1 1 0 1 1 0 1 0 1 0 0 0 1 0 1 1 0 1 0 1 0 1 1 0 1 0 0 1 1 1 0 0 1 0 1 1 0 1 0 1 1
  //   4*0 1 0 0 1 0 1 1 0 1 0 1 1 6*0 1 1 0 1 0 1 0 1 1 0 1 0 0 1 0 1 1 0 1 0 1 1 6*0 1 1 0 1 0 1 0 1 1 0
  //   1 1 6*0 1 1 0 1 0 1 0 1 1 0 1 1 0 0 1 0 1 1 0 1 0 1 0 1 1 0 1 1 0 1 0 1 0 1 1 0 1 0 1 1 0 0 0 1 1 0
  //   0 4*1 0 1 1 0 1 0 1 0 1 0 1 1 0 1 1 0 1 0 1 1 1 0 1 1 0 1 1 0 1 0 1 0 1 1 0 1 1 0 0 4*1 0 0 0 1 6*0
  //   1 1 0 1 1 0 1 0 0 1 1 0 1 0 1 0 1 1 0 1 1 0 1 0 1 0 1 1 0 1 0 1 1 0 0 0 1 1 0 0 1 1 0 1 0 1 0 1 1 0
  //   1 1 0 0 1 0 1 1 0 1 0 4*1 0 0 0 1 0 1 1 0 1 0 1 1 6*0 1 1 0 5*1 0 1 1 1 0 1 0 1 1 1 0 0 1 0 1 0 1 0
  //   1 0 0 1 1 1 0 1 0 1 0 0 1 1 0 5*1 5*0 1 0 0 0 1 0 0 1 0 1 1 0 1 0 1 1 0 1 0 1 1 0 0 0 1 1 0 1 0 1 1
  //   1 0 1 0 1 0 1 1 0 1 1 5*0 1 1 1 0 1 0 5*1 0 1 0 1 0 1 1 0 1 1 4*0 1 1 6*0 1 0 1 1 0 0 7*1 0 1 0 1 0
  //   0 1 1 0 0 1 1 0 1 0 1 0 1 1 0 1 1 0 0 0 1 1 1 0 4*1 0 1 0 1 0 1 1 0 1 1 0 0 1 1 0 0 0 1 1 0 0 1 0 1
  //   1 0 1 0 1 1 0 0 0 1 1 0 1 0 1 0 1 0 1 1 0 1 0 1 0 1 1 0 1 0 1 0 0 1 1 0 1 0 0 6*1 0 1 0 1 0 0 1 0 1
  //   1 0 0 1 0 1 0 1 1 0 0 4*1 0 1 1 0 1 0 1 0 1 0 0 1 1 0 1 0 1 0 1 0 1 1 0 0 1 0 1 1 0 0 1 1 0 1 0 1 0
  //   0 1 1 0 1 1 0 0 1 1 1 0 1 0 1 1 0 0 1 0 1 1 0 1 0 1 1 5*0 1 1 1 0 1 0 1 0 1 1 0 1 1 0 0 0 1 1 5*0
  //   4*1 0 0 1 0 0 0 1 1 0 1 0 1 0 1 0 1 0 1 1 0 1 0 1 0 1 0 0 1 1 0 0 1 1 1 0 1 0 1 0 1 0 4*1 0 1 0 1 1
  //   0 1 0 1 1 0 0 0 1 1 0 1 0 1 0 1 0 1 1 0 1 0 1 1 0 0 0 1 1 1 0 1 1 1 0 0 0 1 0 0 1 0 1 1 1
  //   Expected Outputs
  //   contents of rom_2 (hex, n*v repeats v):
  //   6d 77 3c 6a 5d 56 71 2e 61 63 4e 5a 46 4c 4b 4f 21 68 2b 76 3b 60 79 4e 64 28 2b 59 4b 57 6d 29 5b
  //   57 5b 3c 3b 23 3a 73 59 55 3f 34 68 7d 6b 23 3a 3b 4f 5b 31 6e 44 64 65 20 68 76 61 22 27 79 5d 37
  //   7a 69 2a 5e 31 3f 77 22 42 5f 32 45 74 7a 73 53 59 7a 7e 78 5c 5e 37 73 63 48 53 74 51 22 26 6d 72
  //   79
endmodule

module HUFFDEC (
  input  X,
  input  [16:0] DATA,
  input  CLK,
  input  RST,
  input  X_VAL,
  input  ADDR_RDY,
  input  DATA_VAL,
  input  CHAR_RDY,
  output [7:0] ADDR,
  output [7:0] CHAR,
  output X_RDY,
  output ADDR_VAL,
  output DATA_RDY,
  output CHAR_VAL
);

  wire ADDR_VAL_t, and_2_out, and_4_out, and_6_out, and_8_out, and_12_out, and_13_out, comparator_2_eq,
       comparator_4_eq, comparator_6_eq, comparator_8_eq, comparator_10_eq, DATA_VAL_star, DEC_1, DEC_2,
       DEC_3, DEC_4, DEC_5, FREE_1, FREE_2, FREE_3, FREE_4, FREE_5, huffdec_control_1_addr_en,
       huffdec_control_1_root, MATCH, priority_encoder_1_gs, STORE, STR_1, STR_2, STR_3, STR_4, STR_5;
  wire [2:0] priority_encoder_1_out, SLCT;
  wire [3:0] PTAG_1, PTAG_2, PTAG_3, PTAG_4, PTAG_5;
  wire [7:0] multiplexer_2_out, multiplexer_3_out;
  wire [16:0] DATA_1, DATA_2, DATA_3, DATA_4, DATA_5, FINAL_DATA, PDATA;
  wire [16:8] register_1_q;

  Multiplexer #(.select(3), .width(17), .enable("false")) multiplexer_1 (
    .in0(DATA_1), .in1(DATA_2), .in2(DATA_3), .in3(DATA_4), .in4(DATA_5), .out(PDATA), .sel(SLCT));  // open: in5, in6, in7
  RAM #(.addrWidth(4), .dataWidth(21), .bus("separate")) ram_1 (
    .addr(ADDR[3:0]), .din({DATA, ADDR[7:4]}), .data({DATA_1, PTAG_1}), .str(STR_1), .clk(CLK), .clr(RST));  // open: sel, ld
  and and_1 (STR_1, DEC_1, STORE);
  Comparator #(.width(21)) comparator_1 (.a({DATA_1, PTAG_1}), .b({21{1'b0}}), .eq(FREE_1));  // open: gt, lt
  and and_2 (and_2_out, ~FREE_1, comparator_2_eq);  // AND_Gate
  Comparator #(.width(4)) comparator_2 (.a(PTAG_1), .b(ADDR[7:4]), .eq(comparator_2_eq));  // open: gt, lt
  HUFFDEC_CONTROL huffdec_control_1 (
    .CLK(CLK), .RST(RST), .X_VAL(X_VAL), .ADDR_RDY(ADDR_RDY), .DATA_VAL(DATA_VAL_star),
    .LEAF(FINAL_DATA[16]), .CHAR_RDY(CHAR_RDY), .ADDR_EN(huffdec_control_1_addr_en), .X_RDY(X_RDY),
    .ADDR_VAL(ADDR_VAL_t), .DATA_RDY(DATA_RDY), .CHAR_VAL(CHAR_VAL), .ROOT(huffdec_control_1_root));
  and and_3 (STR_2, DEC_2, STORE);
  Comparator #(.width(21)) comparator_3 (.a({DATA_2, PTAG_2}), .b({21{1'b0}}), .eq(FREE_2));  // open: gt, lt
  Comparator #(.width(4)) comparator_4 (.a(PTAG_2), .b(ADDR[7:4]), .eq(comparator_4_eq));  // open: gt, lt
  Register #(.width(17)) register_1 (.D(FINAL_DATA), .en(DATA_RDY), .Q({register_1_q, CHAR}), .clk(CLK), .clr(RST));
  RAM #(.addrWidth(4), .dataWidth(21), .bus("separate")) ram_2 (
    .addr(ADDR[3:0]), .din({DATA, ADDR[7:4]}), .data({DATA_2, PTAG_2}), .str(STR_2), .clk(CLK), .clr(RST));  // open: sel, ld
  and and_4 (and_4_out, ~FREE_2, comparator_4_eq);  // AND_Gate
  Multiplexer #(.width(8), .enable("false")) multiplexer_2 (
    .in0(register_1_q[15:8]), .in1(CHAR), .out(multiplexer_2_out), .sel(X));
  RAM #(.addrWidth(4), .dataWidth(21), .bus("separate")) ram_3 (
    .addr(ADDR[3:0]), .din({DATA, ADDR[7:4]}), .data({DATA_3, PTAG_3}), .str(STR_3), .clk(CLK), .clr(RST));  // open: sel, ld
  and and_5 (STR_3, DEC_3, STORE);
  Comparator #(.width(21)) comparator_5 (.a({DATA_3, PTAG_3}), .b({21{1'b0}}), .eq(FREE_3));  // open: gt, lt
  Comparator #(.width(4)) comparator_6 (.a(PTAG_3), .b(ADDR[7:4]), .eq(comparator_6_eq));  // open: gt, lt
  or or_1 (DATA_VAL_star, DATA_VAL, MATCH);
  Multiplexer #(.width(8), .enable("false")) multiplexer_3 (
    .in0(multiplexer_2_out), .in1({8{1'b0}}), .out(multiplexer_3_out), .sel(huffdec_control_1_root));
  and and_6 (and_6_out, ~FREE_3, comparator_6_eq);  // AND_Gate
  Multiplexer #(.width(17), .enable("false")) multiplexer_4 (.in0(DATA), .in1(PDATA), .out(FINAL_DATA), .sel(MATCH));
  Register register_2 (.D(multiplexer_3_out), .en(huffdec_control_1_addr_en), .Q(ADDR), .clk(CLK), .clr(RST));
  and and_7 (STR_4, DEC_4, STORE);
  Comparator #(.width(21)) comparator_7 (.a({DATA_4, PTAG_4}), .b({21{1'b0}}), .eq(FREE_4));  // open: gt, lt
  Comparator #(.width(4)) comparator_8 (.a(PTAG_4), .b(ADDR[7:4]), .eq(comparator_8_eq));  // open: gt, lt
  RAM #(.addrWidth(4), .dataWidth(21), .bus("separate")) ram_4 (
    .addr(ADDR[3:0]), .din({DATA, ADDR[7:4]}), .data({DATA_4, PTAG_4}), .str(STR_4), .clk(CLK), .clr(RST));  // open: sel, ld
  and and_8 (and_8_out, ~FREE_4, comparator_8_eq);  // AND_Gate
  and and_9 (ADDR_VAL, ~MATCH, ADDR_VAL_t);  // AND_Gate
  RAM #(.addrWidth(4), .dataWidth(21), .bus("separate")) ram_5 (
    .addr(ADDR[3:0]), .din({DATA, ADDR[7:4]}), .data({DATA_5, PTAG_5}), .str(STR_5), .clk(CLK), .clr(RST));  // open: sel, ld
  and and_10 (STR_5, DEC_5, STORE);
  Comparator #(.width(21)) comparator_9 (.a({DATA_5, PTAG_5}), .b({21{1'b0}}), .eq(FREE_5));  // open: gt, lt
  Comparator #(.width(4)) comparator_10 (.a(PTAG_5), .b(ADDR[7:4]), .eq(comparator_10_eq));  // open: gt, lt
  and and_11 (STORE, ~MATCH, DATA_VAL);  // AND_Gate
  Priority_Encoder priority_encoder_1 (
    .in0(FREE_1), .in1(FREE_2), .in2(FREE_3), .in3(FREE_4), .in4(FREE_5), .out(priority_encoder_1_out),
    .gs(priority_encoder_1_gs));  // open: in5, in6, in7, en_in, en_out
  and and_12 (and_12_out, ~FREE_5, comparator_10_eq);  // AND_Gate
  Priority_Encoder #(.disabled(0)) priority_encoder_2 (
    .in0(and_2_out), .in1(and_4_out), .in2(and_6_out), .in3(and_8_out), .in4(and_12_out), .out(SLCT),
    .gs(MATCH));  // open: in5, in6, in7, en_in, en_out
  Decoder #(.select(3), .disabled(0)) decoder_1 (
    .out0(DEC_1), .out1(DEC_2), .out2(DEC_3), .out3(DEC_4), .out4(DEC_5), .sel(priority_encoder_1_out),
    .en(and_13_out));  // open: out5, out6, out7
  and and_13 (and_13_out, STORE, priority_encoder_1_gs, DATA_VAL);

  // Other names for the same wires on the sheet: TAG[3:0] = ADDR[7:4]; ADDR_VAL_star = ADDR_VAL;
  //   LEAF = FINAL_DATA[16]; ROUT_1[20:0] = {DATA_1, PTAG_1}; TAG_1[3:0] = PTAG_1; PDATA_1[16:0] = DATA_1;
  //   ROUT_2[20:0] = {DATA_2, PTAG_2}; TAG_2[3:0] = PTAG_2; PDATA_2[16:0] = DATA_2; ROUT_3[20:0] = {DATA_3, PTAG_3};
  //   TAG_3[3:0] = PTAG_3; PDATA_3[16:0] = DATA_3; ROUT_4[20:0] = {DATA_4, PTAG_4}; TAG_4[3:0] = PTAG_4;
  //   PDATA_4[16:0] = DATA_4; ROUT_5[20:0] = {DATA_5, PTAG_5}; TAG_5[3:0] = PTAG_5; PDATA_5[16:0] = DATA_5
endmodule

module HUFFDEC_CONTROL (
  input  CLK,
  input  RST,
  input  X_VAL,
  input  ADDR_RDY,
  input  DATA_VAL,
  input  LEAF,
  input  CHAR_RDY,
  output CHAR_VAL,
  output DATA_RDY,
  output ADDR_VAL,
  output X_RDY,
  output ROOT,
  output ADDR_EN
);

  wire and_1_out, and_2_out, and_3_out, and_4_out, and_5_out, and_6_out, and_7_out, and_8_out;
  wire [2:0] D0_out, register_1_q;

  Register #(.width(3)) register_1 (.D(D0_out), .Q(register_1_q), .clk(CLK), .clr(RST));  // open: en
  Decoder #(.select(3), .enable("false")) decoder_1 (
    .out0(ROOT), .out1(X_RDY), .out2(ADDR_VAL), .out3(DATA_RDY), .out4(CHAR_VAL), .sel(register_1_q));  // open: out5, out6, out7
  and and_1 (and_1_out, DATA_RDY, DATA_VAL, LEAF);
  and and_2 (and_2_out, CHAR_VAL, ~CHAR_RDY);  // AND_Gate
  or D2 (D0_out[2], and_1_out, and_2_out);
  and and_3 (and_3_out, X_RDY, X_VAL);
  and and_4 (and_4_out, DATA_RDY, ~DATA_VAL);  // AND_Gate
  or D1 (D0_out[1], and_3_out, ROOT, ADDR_VAL, and_4_out);
  and and_5 (and_5_out, ADDR_VAL, ADDR_RDY);
  and and_6 (and_6_out, X_RDY, ~X_VAL);  // AND_Gate
  and and_7 (and_7_out, DATA_RDY, ~DATA_VAL);  // AND_Gate
  and and_8 (and_8_out, DATA_RDY, DATA_VAL, ~LEAF);  // AND_Gate
  or D0 (D0_out[0], and_6_out, and_5_out, and_7_out, and_8_out);
  or or_1 (ADDR_EN, ROOT, X_RDY);

  // Notes on the sheet:
  //   OFFER_CHAR
  //   WAIT_DATA
  //   OFFER_ADDR
  //   WAIT_X
  //   INIT_CHAR
endmodule

module SLOW_TREE_ROM (
  input  [7:0] ADDR,
  input  CLK,
  input  RST,
  input  DATA_RDY,
  input  ADDR_VAL,
  output [16:0] DATA,
  output ADDR_RDY,
  output DATA_VAL
);

  wire comparator_1_eq, slow_tree_rom_cntl_1_accept;
  wire [3:0] counter_1_q;
  wire [7:0] register_1_q;
  wire [16:0] rom_1_data;

  Counter #(.width(4), .max('hf)) counter_1 (
    .Q(counter_1_q), .clk(CLK), .clr(slow_tree_rom_cntl_1_accept));  // open: load, D, count, carry
  Comparator #(.width(4)) comparator_1 (.a(4'b0111), .b(counter_1_q), .eq(comparator_1_eq));  // open: gt, lt
  SLOW_TREE_ROM_CNTL slow_tree_rom_cntl_1 (
    .CLK(CLK), .RST(RST), .RES_RDY(DATA_RDY), .DONE(comparator_1_eq), .CMD_VAL(ADDR_VAL), .READY(ADDR_RDY),
    .ACCEPT(slow_tree_rom_cntl_1_accept), .OFFER(DATA_VAL));  // open: PROCESS
  Register register_1 (.D(ADDR), .en(ADDR_RDY), .Q(register_1_q), .clk(CLK), .clr(RST));
  ROM #(.dataWidth(17)) rom_1 (.addr(register_1_q), .data(rom_1_data));  // open: sel
  Multiplexer #(.width(17), .disabled(0), .enable("false")) multiplexer_1 (
    .in0({17{1'b1}}), .in1(rom_1_data), .out(DATA), .sel(DATA_VAL));

  // Notes on the sheet:
  //   contents of rom_1 (hex, n*v repeats v):
  //   bbbc 10020 10024 10028 1002c 10030 10034 10038 1003c 10040 10044 10048 1004c 10050 10054 10058 1005c
  //   10060 10064 10068 1006c 10070 10074 10078 1007c 10023 10027 1002b 1002f 10033 10037 1003b 1003f
  //   10043 10047 1004b 1004f 10053 10057 1005b 1005f 10063 10067 1006b 1006f 10073 10077 1007b 10022
  //   10026 1002a 1002e 10032 10036 1003a 1003e 10042 10046 1004a 1004e 10052 10056 1005a 1005e 10062
  //   10066 1006a 1006e 10072 10076 1007a 1007e 10021 10025 10029 1002d 10031 10035 10039 1003d 10041
  //   10045 10049 1004d 10051 10055 10059 1005d 10061 10065 10069 1006d 10071 10075 10079 1007d 181a 2f30
  //   3760 6103 862 3663 6457 2710 4a11 6531 4f47 4901 663f 1f20 6768 1b69 6a1c 46b 6c6d 6e6f 7071 7219
  //   7302 2874 f54 753e 764b 3d09 3277 5678 4833 2679 553a 7a39 237b 7c22 b7d 7e7f 210a 5280 240d 3b0c
  //   530e 3881 3c82 5183 2584 8550 8687 8889 8a8b 8c8d 8e8f 9091 925c 9394 1795 4696 4542 9798 2e41 995e
  //   1e07 9a35 4e2a 4d06 2b9b 5d40 131d 159c 2905 129d 5b34 9e9f a014 a116 a24c a343 2d5a a4a5 442c a6a7
  //   5fa8 a959 aa58 abac adae afb0 b1b2 b3b4 b5b6 b7b8 b9ba
endmodule

module SLOW_TREE_ROM_CNTL (
  input  CLK,
  input  RST,
  input  RES_RDY,
  input  DONE,
  input  CMD_VAL,
  output READY,
  output ACCEPT,
  output PROCESS,
  output OFFER
);

  wire and_1_out, and_2_out, and_3_out;
  wire [1:0] d0_out, register_1_q;

  Register #(.width(2)) register_1 (.D(d0_out), .Q(register_1_q), .clk(CLK), .clr(RST));  // open: en
  Decoder #(.select(2), .disabled(0), .enable("false")) decoder_1 (
    .out0(READY), .out1(ACCEPT), .out2(PROCESS), .out3(OFFER), .sel(register_1_q));
  or d1 (d0_out[1], ACCEPT, PROCESS, and_1_out);
  and and_1 (and_1_out, ~RES_RDY, OFFER);  // AND_Gate
  and and_2 (and_2_out, DONE, PROCESS);
  or d0 (d0_out[0], and_1_out, and_2_out, and_3_out);
  and and_3 (and_3_out, CMD_VAL, READY);
endmodule
