// Logisim project scaffolding.circ as structural Verilog: 2 circuits, main circuit main
// HALT
module main (
  output [23:0] NUM_PASS,
  output [23:0] NUM_FAIL,
  output DONE,
  output halt
);

  wire CLK, comparator_1_eq, not_1_out, RST;
  wire [4:0] caesar_1_out, rom_1_data, rom_2_data;
  wire [23:0] adder_1_out, stepper_1_value, stepper_2_value;

  Clock clock_1 (.out(CLK));
  Button button_1 (.out(RST));
  STEPPER stepper_1 (.ADVANCE(1'b1), .CLK(CLK), .RST(RST), .VALUE(stepper_1_value), .HALT(DONE));
  ROM #(.addrWidth(24), .dataWidth(5)) rom_1 (.addr(stepper_1_value), .data(rom_1_data));  // open: sel
  STEPPER stepper_2 (.ADVANCE(1'b1), .CLK(CLK), .RST(RST), .VALUE(stepper_2_value), .HALT(DONE));
  CAESAR caesar_1 (.IN(rom_1_data), .OUT(caesar_1_out));
  ROM #(.addrWidth(24), .dataWidth(5)) rom_2 (.addr(stepper_2_value), .data(rom_2_data));  // open: sel
  Comparator #(.width(5)) comparator_1 (.a(caesar_1_out), .b(rom_2_data), .eq(comparator_1_eq));  // open: gt, lt
  not not_1 (not_1_out, comparator_1_eq);
  STEPPER stepper_3 (.ADVANCE(comparator_1_eq), .CLK(CLK), .RST(RST), .VALUE(NUM_PASS), .HALT(DONE));
  STEPPER stepper_4 (.ADVANCE(not_1_out), .CLK(CLK), .RST(RST), .VALUE(NUM_FAIL), .HALT(DONE));
  Adder #(.width(24)) adder_1 (.a(NUM_FAIL), .b(NUM_PASS), .out(adder_1_out));  // open: cin, cout
  TRIGGER trigger_1 (.INPUT(adder_1_out), .TRIGGER(24'h1a), .CLK(CLK), .RST(RST), .TRIGGERED(DONE));

  assign halt = DONE;

  // Notes on the sheet:
  //   Test Inputs
  //   contents of rom_1 (hex, n*v repeats v):
  //   10 6 16 1e 8 e a 1a c 12 13 1b b f 1c 1f 17 7 5 15 14 1d d 9 4 19
  //   Expected Outputs
  //   contents of rom_2 (hex, n*v repeats v):
  //   a 1a c 12 13 1b b f 1c 1f 17 7 5 15 14 1d d 9 4 19 10 6 16 1e 8 e
  //   # Tests:
endmodule

module CAESAR (
  input  [4:0] IN,
  output [4:0] OUT
);


  assign OUT = IN;
endmodule
