// Logisim project scaffolding.circ as structural Verilog: 2 circuits, main circuit main
// HALT
module main (
  output [23:0] NUM_PASS,
  output [23:0] NUM_FAIL,
  output DONE,
  output TIMEOUT,
  output halt
);

  wire and_1_out, and_2_out, and_3_out, and_4_out, and_5_out, and_6_out, CLK, comparator_1_eq,
       replicator_1_rdy_out, replicator_1_val_out, RST;
  wire [1:0] random_1_out, replicator_1_data_out, rom_1_data, rom_2_data;
  wire [23:0] adder_1_out, stepper_1_value, stepper_2_value, stepper_5_value;

  Clock clock_1 (.out(CLK));
  Button button_1 (.out(RST));
  STEPPER stepper_1 (.ADVANCE(and_1_out), .CLK(CLK), .RST(RST), .VALUE(stepper_1_value), .HALT(halt));
  ROM #(.addrWidth(24), .dataWidth(2)) rom_1 (.addr(stepper_1_value), .data(rom_1_data));  // open: sel
  and and_1 (and_1_out, and_2_out, replicator_1_rdy_out);
  and and_2 (and_2_out, ~halt, random_1_out[1]);  // AND_Gate
  REPLICATOR replicator_1 (
    .RDY_OUT(replicator_1_rdy_out), .CLK(CLK), .RST(RST), .DATA_IN(rom_1_data), .VAL_IN(and_2_out),
    .DATA_OUT(replicator_1_data_out), .VAL_OUT(replicator_1_val_out), .RDY_IN(and_3_out));
  Random #(.width(2)) random_1 (.clk(CLK), .out(random_1_out));  // open: next, clr
  and and_3 (and_3_out, random_1_out[0], ~halt);  // AND_Gate
  and and_4 (and_4_out, replicator_1_val_out, and_3_out);
  STEPPER stepper_2 (.ADVANCE(and_4_out), .CLK(CLK), .RST(RST), .VALUE(stepper_2_value), .HALT(halt));
  ROM #(.addrWidth(24), .dataWidth(2)) rom_2 (.addr(stepper_2_value), .data(rom_2_data));  // open: sel
  Comparator #(.width(2)) comparator_1 (
    .a(replicator_1_data_out), .b(rom_2_data), .eq(comparator_1_eq));  // open: gt, lt
  and and_5 (and_5_out, and_4_out, comparator_1_eq);
  and and_6 (and_6_out, ~comparator_1_eq, and_4_out);  // AND_Gate
  STEPPER stepper_3 (.ADVANCE(and_5_out), .CLK(CLK), .RST(RST), .VALUE(NUM_PASS), .HALT(halt));
  STEPPER stepper_4 (.ADVANCE(and_6_out), .CLK(CLK), .RST(RST), .VALUE(NUM_FAIL), .HALT(halt));
  Adder #(.width(24)) adder_1 (.a(NUM_FAIL), .b(NUM_PASS), .out(adder_1_out));  // open: cin, cout
  STEPPER stepper_5 (.ADVANCE(1'b1), .CLK(CLK), .RST(RST), .VALUE(stepper_5_value), .HALT(halt));
  TRIGGER trigger_1 (.INPUT(adder_1_out), .TRIGGER(24'h18), .CLK(CLK), .RST(RST), .TRIGGERED(DONE));
  TRIGGER trigger_2 (.INPUT(stepper_5_value), .TRIGGER(24'h960), .CLK(CLK), .RST(RST), .TRIGGERED(TIMEOUT));
  or or_1 (halt, DONE, TIMEOUT);

  // Notes on the sheet:
  //   Test Inputs
  //   contents of rom_1 (hex, n*v repeats v):
  //   0 2 3 0 2 2 0 0 2 0 1 3 2 3 2 1 1 0 1 1 3 3 0 1 3 1 0 3 1 2 3 2
  //   Randomly offer/accept data
  //   Expected Outputs
  //   contents of rom_2 (hex, n*v repeats v):
  //   0 0 2 2 1 1 1 4*2 1 3 3 3 0 3 0 0 0 1 1 3 3
  //   # Tests:
  //   Timeout:
endmodule

module REPLICATOR (
  input  [1:0] DATA_IN,
  input  VAL_IN,
  input  RDY_IN,
  input  CLK,
  input  RST,
  output [1:0] DATA_OUT,
  output VAL_OUT,
  output RDY_OUT
);


  assign DATA_OUT = DATA_IN;
  assign RDY_OUT = RDY_IN;
  assign VAL_OUT = VAL_IN;
endmodule
